# Fritzing sketch mcp23017 (saved by Fritzing 0.9.3b)
breadboards: 1

parts:
  Componente1 = Arduino Uno (Rev3)
  IC1 = MCP23017 I2C I/O Expander
  R1 = Resistor [tolerance=±5% resistance=4.7k package=THT]
  LED1 = LED - 5mm [color="Red (633nm)" package="5 mm [THT]"]
  LED2 = LED - 5mm [color="Red (633nm)" package="5 mm [THT]"]

nets:
  N1: Componente1.A4/SDA, IC1.SDA
  N2: Componente1.A5/SCL, IC1.SCL
  5V: Componente1.5V, IC1.VDD
  GND: Componente1.GND, IC1.VSS, LED1.cathode
  N3: IC1.GPB0, LED1.anode
  N4: IC1.A0, IC1.A1, IC1.A2, LED2.cathode
  N5: IC1.RESET, R1.Pin_0
  N6: IC1.GPA0, LED2.anode

custom parts:
  MCP23017 I2C I/O Expander: The MCP23017 uses two i2c pins (these can be shared with other i2c devices), and in exchange gives you 16 general purpose pins. You can set each of 16 pins to be input, output, input with a pullup or open drain. There's even the ability to get an interrupt via an external pin when any of the inputs change so you don't have to keep polling the chip.
